# Fritzing sketch drumosc (saved by Fritzing 0.9.10b)
breadboards: 1

parts:
  S2 = Pushbutton [package="[THT]"]
  R1 = Rotary Potentiometer (Small) [maximum_resistance=100kΩ knob_status=50% power=0.5W package=THT]  # not connected
  S1 = Pushbutton [package="[THT]"]
  SP1 = SPEAKER [package=pcb_mount_speaker]
  SOM1 = DaisySeed [chip_label=IC]

nets:
  N1: S2.Pin_1, S2.Pin_2, S1.Pin_1, S1.Pin_2, SP1.+, SOM1.connector20
  N2: S2.Pin_3, S2.Pin_4, SOM1.connector35
  N3: S1.Pin_3, S1.Pin_4, SOM1.connector34
  N4: SP1.-, SOM1.connector19
